// Logisim project ANDORCir.circ as structural Verilog: 1 circuit, main circuit main
module main (
  input  A,
  input  B,
  input  C
);

  wire ABC_out, ABnC_out, ABnCn_out, AnBC_out, AnBnC_out, not_1_out, not_2_out, not_3_out, or_1_out;

  not not_1 (not_1_out, A);
  not not_2 (not_2_out, B);
  not not_3 (not_3_out, C);
  and ABC (ABC_out, A, B, C);
  and AnBC (AnBC_out, not_1_out, B, C);
  and ABnCn (ABnCn_out, A, not_2_out, not_3_out);
  and ABnC (ABnC_out, A, not_2_out, C);
  and AnBnC (AnBnC_out, not_1_out, not_2_out, C);
  or or_1 (or_1_out, ABC_out, AnBC_out, ABnCn_out, ABnC_out, AnBnC_out);
  LED led_1 (.in(or_1_out));
endmodule
