// Logisim project NANDCir.circ as structural Verilog: 1 circuit, main circuit main
module main (
  input  A,
  input  B,
  input  C
);

  wire ABC_out, ABnC_out, ABnCn_out, An_out, AnBC_out, AnBnC_out, Bn_out, Cn_out, nand_1_out;

  nand An (An_out, A, A);
  nand Bn (Bn_out, B, B);
  nand Cn (Cn_out, C, C);
  nand ABC (ABC_out, A, B, C);
  nand AnBC (AnBC_out, An_out, B, C);
  nand ABnCn (ABnCn_out, A, Bn_out, Cn_out);
  nand ABnC (ABnC_out, A, Bn_out, C);
  nand AnBnC (AnBnC_out, An_out, Bn_out, C);
  nand nand_1 (nand_1_out, ABC_out, AnBC_out, ABnCn_out, ABnC_out, AnBnC_out);
  LED led_1 (.in(nand_1_out));
endmodule
